# Fritzing sketch ThermoTweet (saved by Fritzing 0.9.3b)
breadboards: 1

parts:
  Raspberry_Pi_1 = Raspberry Pi 3 [part_number=RPI-3-V1.2]
  J1 = T Cobbler Plus
  DS1 = DS18B20 1-Wire Temperature Sensor [part_number=DS18B20]
  R1 = Resistor [tolerance=±5% resistance=4.7k package=THT]
  LCD1 = LCD screen
  R2 = Resistor [tolerance=±5% resistance=1.5k package=THT]

nets:
  3V3: Raspberry_Pi_1.3v3, Raspberry_Pi_1.3V3, J1.3.3V#41, J1.3.3V#57
  N1: Raspberry_Pi_1.GPIO2, J1.GPIO_2
  N2: Raspberry_Pi_1.GPIO3, J1.GPIO_3
  N3: Raspberry_Pi_1.GPIO4, J1.GPIO_4
  N4: Raspberry_Pi_1.GND, J1.GND#46, J1.GND#49, J1.GND#54, J1.GND#60, J1.GND#65, J1.GND#70, J1.GND#74, J1.GND#79
  N5: Raspberry_Pi_1.GPIO17, J1.GPIO_17
  N6: Raspberry_Pi_1.GPIO27, J1.GPIO_27
  N7: Raspberry_Pi_1.GPIO22, J1.GPIO_22
  N8: Raspberry_Pi_1.GPIO10, J1.GPIO_10
  N9: Raspberry_Pi_1.GPIO9, J1.GPIO_9
  N10: Raspberry_Pi_1.GPIO11, J1.GPIO_11
  N11: Raspberry_Pi_1.ID_SD, J1.ID_SD
  N12: Raspberry_Pi_1.GPIO5, J1.GPIO_5
  N13: Raspberry_Pi_1.GPIO6, J1.GPIO_6
  N14: Raspberry_Pi_1.GPIO13, J1.GPIO_13
  N15: Raspberry_Pi_1.GPIO19, J1.GPIO_19
  N16: Raspberry_Pi_1.GPIO26, J1.GPIO_26
  N17: Raspberry_Pi_1.GPIO21, J1.GPIO_21
  N18: Raspberry_Pi_1.GPIO20, J1.GPIO_20
  N19: Raspberry_Pi_1.GPIO16, J1.GPIO_16
  N20: Raspberry_Pi_1.GPIO12, J1.GPIO_12
  N21: Raspberry_Pi_1.ID_SC, J1.ID_SC
  N22: Raspberry_Pi_1.GPIO7, J1.GPIO_7
  N23: Raspberry_Pi_1.GPIO8, J1.GPIO_8
  N24: Raspberry_Pi_1.GPIO25, J1.GPIO_25
  N25: Raspberry_Pi_1.GPIO24, J1.GPIO_24
  N26: Raspberry_Pi_1.GPIO23, J1.GPIO_23
  N27: Raspberry_Pi_1.GPIO18, J1.GPIO_18
  N28: Raspberry_Pi_1.GPIO15, J1.GPIO_15
  N29: Raspberry_Pi_1.GPIO14, J1.GPIO_14
  5V: Raspberry_Pi_1.5V, J1.5V
  3V3_2: J1.3V3, DS1.VDD, R1.Pin_1
  N30: J1.5.0V#1, LCD1.VDD, LCD1.LED+
  GND: J1.GND#5, J1.GND#8, DS1.GND, LCD1.VSS, LCD1.R/W, LCD1.LED-, R2.Pin_0
  N31: J1.#4, DS1.DQ, R1.Pin_0
  N32: J1.#17, LCD1.DB5
  N33: J1.#18, LCD1.DB6
  N34: J1.#22, LCD1.DB7
  N35: J1.#23, LCD1.DB4
  N36: J1.#24, LCD1.E
  N37: J1.#25, LCD1.RS
  N38: LCD1.V0, R2.Pin_1

custom parts:
  T Cobbler Plus: The T-Cobbler Plus is an add on prototyping board from Adafruit specifically designed for the Raspberry Pi B+ that can break out all those tasty power, GPIO, I2C and SPI pins from the 40-pin header onto a solderless breadboard. This set will make "cobbling together" prototypes with the Pi super easy. The T-Cobbler Plus can plug into any solderless breadboard.
